# Fritzing sketch Relay-Checker (saved by Fritzing 0.9.3b)

parts:
  Part1 = Arduino Uno (Rev3)
  U1 = 4-Channel 5v Relay Shield [package=relay-4ch5v10a]

nets:
  N1: Part1.D9_PWM, U1.IN4
  N2: Part1.D10_PWM/SS, U1.IN3
  N3: Part1.D11_PWM/MOSI, U1.IN2
  N4: Part1.D12/MISO, U1.IN1
  GND: Part1.GND, U1.GND
  5V: Part1.5V, U1.VCC

custom parts:
  4-Channel 5v Relay Shield: 4 Channel 5v Relay Shield w. 2x SPD-06VDC-SD-C
